# Fritzing sketch pcb (saved by Fritzing 0.9.3b)
circuit board: 6cm x 6cm
breadboards: 1

parts:
  J1 = female pin header, 5 pins [form="♀ (female)"]
  J13 = double row female pin header, 4 pins [form="♀ (female)"]
  U4 = Sharp PC817 [package=THT]
  D1 = Rectifier Diode [part_number=1N4001 package="300 mil [THT]"]
  LED = female pin header, 2 pins [form="♀ (female)"]
  LED1 = LED - 5mm [color="Red (633nm)" package="5 mm [THT]"]
  R12 = Resistor [tolerance=±5% resistance=150 package="1206 [SMD]"]
  R11 = Resistor [tolerance=±5% resistance=220 package="1206 [SMD]"]
  U2 = Voltage Regulator LM1117 [package=sot223]
  R2 = Resistor [tolerance=±5% resistance=10k package="1206 [SMD]"]
  R13 = Resistor [tolerance=±5% resistance=10k package="1206 [SMD]"]
  R9 = Resistor [tolerance=±5% resistance=10k package="1206 [SMD]"]
  R10 = Resistor [tolerance=±5% resistance=10k package="1206 [SMD]"]
  R1 = Resistor [tolerance=±5% resistance=10k package="1206 [SMD]"]
  R3 = Resistor [tolerance=±5% resistance=10k package="1206 [SMD]"]
  S1 = Toggle Switch [package=THT]
  C1 = Electrolytic Capacitor [capacitance=100µF package="100 mil [THT, electrolytic]"]
  J14 = Camdenboss CTB0158-2 [part_number=CTB0158-2 package=THT]
  U3 = ESP8266 WiFi Module [part_number=ESP8266]
  RC522 = Generic female header - 8 pins [form="♀ (female)" package=THT]
  Limit = female pin header, 2 pins [form="♀ (female)"]
  Push = double row female pin header, 2 pins [form="♀ (female)"]
  OMRON1 = OMRON PCB Power Relay – G5LE [part_number="G5LE-1\n" package=THT]
  R14 = Resistor [tolerance=±5% resistance=100 package="1206 [SMD]"]
  J15 = Camdenboss CTB0158-3 [part_number=CTB0158-3 package=THT]
  C2 = Ceramic Capacitor [capacitance=330nF package="100 mil [THT, multilayer]"]
  Additional_Power = female pin header, 4 pins [form="♀ (female)"]
  C828 = PNP-Transistor [package="TO92 [THT]"]

nets:
  N1: J1.pin1, U3.TXD
  N2: J1.pin2, U3.RXD
  N3: J1.pin3, R1.Pin_1, U3.REST, C2.1
  GND: J1.pin4, J13.pin1, J13.pin4, U2.ADJ, R9.Pin_0, S1.L2, C1.-, J14.pin1, U3.GND, RC522.GND, Limit.pin2, Push.pin2, J15.pin2, C2.0, Additional_Power.pin3, C828.E
  3.3V: J1.pin5, J13.pin2, J13.pin3, LED.pin1, R12.Pin_1, U2.OUT, R2.Pin_0, R13.Pin_1, R10.Pin_1, R1.Pin_0, R3.Pin_0, C1.+, U3.VCC, RC522.3V3, R14.Pin_1, Additional_Power.pin4
  N4: U4.Pin_1, R12.Pin_0
  Relay: U4.Pin_2, U3.GPIO_16
  5V: U4.Pin_4, D1.cathode, U2.IN, J14.pin2, OMRON1.COIL1, OMRON1.C, Additional_Power.pin2
  N5: U4.Pin_3, R11.Pin_0
  N6: D1.anode, OMRON1.COIL2, C828.C
  LED: LED.pin2, LED1.cathode, R10.Pin_0, U3.GPIO_2
  N7: LED1.anode, R14.Pin_0
  N8: R11.Pin_1, C828.B
  N9: R2.Pin_1, U3.CH_PD
  PushBtn: R13.Pin_0, U3.ADC_0, Push.pin1
  N10: R9.Pin_1, U3.GPIO_15
  LimitSW: R3.Pin_1, S1.L1, Limit.pin1
  N11: S1.COM, U3.GPIO_0
  N12: U3.GPIO_4, RC522.SDA
  N13: U3.GPIO_5, RC522.RST
  N14: U3.GPIO_14, RC522.SCK
  N15: U3.GPIO_12, RC522.MISO
  N16: U3.GPIO_13, RC522.MOSI
  N17: OMRON1.A, J15.pin1
  N18: OMRON1.B, J15.pin3

notes:
  PeraRide v1
  Tx,Rx,Rst,GND,3v3
  3v3

custom parts:
  ESP8266 WiFi Module: Generic WiFi Module based on the ESP8266 with onboard PCB antenna and UART communications
  Generic female header - 8 pins: Generic female header
