# Fritzing sketch pcb_v2_nodemcu (saved by Fritzing 0.9.3b)
circuit board: 6cm x 6cm
breadboards: 1

parts:
  D2 = Rectifier Diode [part_number=1N4001 package="300 mil [THT]"]
  R13 = Resistor [tolerance=±5% resistance=220 package="1206 [SMD]"]
  R14 = Resistor [tolerance=±5% resistance=150 package="1206 [SMD]"]
  J16 = Camdenboss CTB0158-3 [part_number=CTB0158-3 package=THT]
  U5 = Sharp PC817 [package=THT]
  J17 = Camdenboss CTB0158-2 [part_number=CTB0158-2 package=THT]
  U6 = Voltage Regulator LM1117 [package=sot223]
  Push1 = double row female pin header, 2 pins [form="♀ (female)"]
  R15 = Resistor [tolerance=±5% resistance=10k package="1206 [SMD]"]
  Limit1 = female pin header, 2 pins [form="♀ (female)"]
  OMRON2 = OMRON PCB Power Relay – G5LE [part_number="G5LE-1\n" package=THT]
  Additional_Power = female pin header, 4 pins [form="♀ (female)"]
  C830 = Electrolytic Capacitor [capacitance=100µF package="100 mil [THT, electrolytic]"]
  J18 = double row female pin header, 4 pins [form="♀ (female)"]
  RC523 = Generic female header - 8 pins [form="♀ (female)" package=THT]
  LED1 = LED - 5mm [color="Red (633nm)" package="5 mm [THT]"]
  R16 = Resistor [tolerance=±5% resistance=220 package="1206 [SMD]"]
  Power = female pin header, 2 pins [form="♀ (female)"]
  C828 = NPN-Transistor [package="TO92 [THT]"]
  U1 = NodeMCU V3.0
  M1 = Dagu DGServo 9g (Top view) [part_number=RS001B]

nets:
  5V: D2.cathode, U5.Pin_4, J17.pin2, U6.IN, OMRON2.COIL1, OMRON2.C, Additional_Power.pin2, Power.pin1, U1.Vin, M1.vcc
  N1: D2.anode, OMRON2.COIL2, C828.C
  N2: R13.Pin_0, U5.Pin_3
  N3: R13.Pin_1, C828.B
  N4: R14.Pin_0, U5.Pin_1
  3.3V: R14.Pin_1, U6.OUT, R15.Pin_1, Additional_Power.pin4, C830.+, J18.pin2, J18.pin3, RC523.3V3, U1.3V3
  N5: J16.pin1, OMRON2.A
  GND: J16.pin2, J17.pin1, U6.ADJ, Push1.pin2, Limit1.pin2, Additional_Power.pin3, C830.-, J18.pin1, J18.pin4, RC523.GND, R16.Pin_0, Power.pin2, C828.E, U1.GND, M1.gnd
  N6: J16.pin3, OMRON2.B
  Relay: U5.Pin_2
  LIMIT: Push1.pin1, R15.Pin_0, U1.A0
  BTN: Limit1.pin1, U1.D3
  RST: RC523.RST, U1.D1
  MISO: RC523.MISO, U1.D6
  MOSI: RC523.MOSI, U1.D7
  SCK: RC523.SCK, U1.D5
  SDA: RC523.SDA, U1.D2
  N7: LED1.cathode, R16.Pin_1
  LED: LED1.anode, U1.D4
  Servo: U1.D0, M1.pulse

notes:
  PeraRide - PCB

custom parts:
  Generic female header - 8 pins: Generic female header
  NodeMCU V3.0: ESP8266 based NodeMCU
